# Fritzing sketch 2-LEDS (saved by Fritzing 1.0.3b)
breadboards: 1

parts:
  LED1 = LED - 5mm [color="Red (633nm)" current=0.030A package="5 mm [THT]"]
  LED2 = LED - 5mm [color="Red (633nm)" current=0.030A package="5 mm [THT]"]
  R1 = Resistor [tolerance=±5% power=0.25W resistance=330k package=THT]
  R2 = Resistor [tolerance=±5% power=0.25W resistance=330k package=THT]
  Raspberry_Pi_1 = Raspberry Pi 3 [part_number=RPI-3-V1.2]

nets:
  N1: LED1.cathode, LED2.cathode, Raspberry_Pi_1.GND
  N2: LED1.anode, R1.Pin_0
  N3: LED2.anode, R2.Pin_0
  N4: R1.Pin_1, Raspberry_Pi_1.GPIO17
  N5: R2.Pin_1, Raspberry_Pi_1.GPIO25

notes:
  GPIO 17
  LED
  Pota llarga + Ànode -> al GPIO de la Rasp
  Pota curta - Càtode -> a GND de la Rasp
  GPIO 25
  GND
